# Fritzing sketch nail2nail (saved by Fritzing 0.9.2b)
breadboards: 1

parts:
  Part1 = Arduino Uno (Rev3)
  R1 = Resistor [tolerance=±5% resistance=220 package=THT]
  ANT1 = Antenna  # not connected
  ANT2 = Antenna
  U1 = Optocoupler [package=THT]
  R2 = Resistor [tolerance=±5% resistance=220 package="0402 [SMD]"]
  U2 = AD22100 - Voltage Output Temperature Sensor with Signal Conditioning [part_number=AD22100]

nets:
  N1: Part1.A0, R1.Pin_0
  N2: Part1.A4/SDA, U1.Pin_2
  N3: Part1.A5/SCL, U1.Pin_1
  N4: Part1.D12/MISO, R2.Pin_1, U2.GND
  N5: Part1.D2, R1.Pin_1
  N6: Part1.D3_PWM, ANT2.antenna_lead
  N7: U1.Pin_3, R2.Pin_0, U2.V+
  N8: U1.Pin_4, U2.Vo

custom parts:
  Optocoupler: Optocoupler - keeps you from frying your stuff!
